# Fritzing sketch Anet LCD Adapter (saved by Fritzing 0.9.3b)
circuit board: 4.23745cm x 2.6258cm
breadboards: 1

parts:
  EXP2 = shrouded pin header, 10 pins [form="♂ (shrouded male)"]
  J3 = shrouded pin header, 10 pins [form="♂ (shrouded male)"]
  LCD = shrouded pin header, 10 pins [form="♂ (shrouded male)"]
  EXP1 = shrouded pin header, 10 pins [form="♂ (shrouded male)"]
  J4 = male pin header, 2 pins [form="♂ (male)"]

nets:
  N1: EXP2.pin1, J3.pin2
  N2: EXP2.pin2, LCD.pin9
  N3: EXP2.pin3, LCD.pin8
  N4: EXP2.pin5, J3.pin7
  N5: EXP2.pin7, J3.pin4
  N6: EXP2.pin8, J3.pin8
  N7: EXP2.pin9, J4.pin1
  N8: EXP2.pin10, J3.pin3
  N9: LCD.pin1, EXP1.pin5
  N10: LCD.pin2, EXP1.pin9
  N11: LCD.pin3, EXP1.pin2
  N12: LCD.pin4, J4.pin2
  N13: LCD.pin5, EXP1.pin3
  N14: LCD.pin6, EXP1.pin1
  N15: LCD.pin7, EXP1.pin10
  N16: LCD.pin10, EXP1.pin6
